// Digital circuit Instruction_Decoder_2.dig as structural Verilog
module Instruction_Decoder_2 (
  input  in_1,
  input  in_2,
  input  in_3,
  input  in_4,
  input  in_5,
  input  in_6,
  input  in_7,
  input  in_8
);

  wire _74540_1_pin11, _74540_1_pin12, _74540_1_pin13, _74540_1_pin14, _74540_1_pin15, _74540_1_pin16,
       _74540_1_pin17, _74540_1_pin18, _74540_2_pin12, _74540_2_pin13, _74540_2_pin14, _74540_2_pin15,
       _74540_2_pin16, _74540_2_pin17, _74540_2_pin18, _74540_3_pin11, _74540_3_pin12, _74540_3_pin13,
       _74540_3_pin14, _74540_3_pin15, _74540_3_pin16, _74540_3_pin17, _74540_3_pin18, _74540_4_pin11,
       _74540_4_pin12, _74540_4_pin13, _74540_4_pin14, _74540_4_pin15, _74540_4_pin16, _74540_4_pin17,
       _74540_4_pin18, _74540_5_pin11, _74540_5_pin12, _74540_5_pin13, _74540_5_pin14, _74540_5_pin15,
       _74540_5_pin16, _74540_5_pin17, _74540_5_pin18, and_2_out, and_3_out, and_4_out, and_5_out, nALUADC,
       nALUADD, nALUAND, nALUCP, nALUOR, nALUSBC, nALUSUB, nALUXOR, nand_2_out, nand_3_out, nC, nM, nNC, nNZ,
       nOPCALLcc, nOPCALLnn, nOPDEC, nOPI_O0, nOPI_O1, nOPI_O2, nOPI_O3, nOPIMMALU, nOPIMMLD, nOPINC,
       nOPJPcc, nOPJPnn, nOPLD, nOPRET, nOPRETcc, nOPRST, nOPSHIFT, not_1_out, not_2_out, not_3_out,
       not_4_out, not_5_out, not_6_out, not_7_out, nP, nPE, nPO, nRDREG_HL, nRDREGA, nRDREGB, nRDREGC,
       nRDREGD, nRDREGE, nRDREGH, nRDREGL, nRLA, nRLCA, nRRA, nRRCA, nTYPE0, nTYPE1, nTYPE2, nTYPE3,
       nWRREG_HL, nWRREGA, nWRREGB, nWRREGC, nWRREGD, nWRREGE, nWRREGH, nWRREGL, nZ;

  _74540 _74540_1 (
    .pin1(1'b0), .pin2(nALUCP), .pin3(nALUOR), .pin4(nALUXOR), .pin5(nALUAND), .pin6(nALUSBC),
    .pin7(nALUSUB), .pin8(nALUADC), .pin9(nALUADD), .pin10(1'b0), .pin11(_74540_1_pin11),
    .pin12(_74540_1_pin12), .pin13(_74540_1_pin13), .pin14(_74540_1_pin14), .pin15(_74540_1_pin15),
    .pin16(_74540_1_pin16), .pin17(_74540_1_pin17), .pin18(_74540_1_pin18), .pin19(1'b0), .pin20(1'b1));
  LED CP (.in(_74540_1_pin18));
  LED OR (.in(_74540_1_pin17));
  LED XOR (.in(_74540_1_pin16));
  not not_1 (not_1_out, nTYPE3);
  LED AND (.in(_74540_1_pin15));
  LED SBC (.in(_74540_1_pin14));
  nand nand_1 (nOPLD, in_7, in_8);
  nand nand_2 (nand_2_out, nTYPE2, nTYPE3);
  and and_2 (and_2_out, nTYPE2, not_1_out);
  LED SUB (.in(_74540_1_pin13));
  LED ADC (.in(_74540_1_pin12));
  and and_3 (and_3_out, in_4, and_2_out);
  and and_4 (and_4_out, in_5, and_2_out);
  and and_5 (and_5_out, in_6, and_2_out);
  LED ADD (.in(_74540_1_pin11));
  LED IMM (.in(not_2_out));
  not not_2 (not_2_out, nOPIMMALU);
  _74540 _74540_2 (
    .pin1(1'b0), .pin2(nOPLD), .pin3(nOPINC), .pin4(nOPDEC), .pin5(nOPJPcc), .pin6(nOPCALLcc),
    .pin7(nOPJPnn), .pin8(nOPCALLnn), .pin9(1'b0), .pin10(1'b0), .pin12(_74540_2_pin12),
    .pin13(_74540_2_pin13), .pin14(_74540_2_pin14), .pin15(_74540_2_pin15), .pin16(_74540_2_pin16),
    .pin17(_74540_2_pin17), .pin18(_74540_2_pin18), .pin19(1'b0), .pin20(1'b1));  // open: pin11
  LED LD (.in(_74540_2_pin18));
  LED INC (.in(_74540_2_pin17));
  _74138 _74138_1 (
    .pin1(in_1), .pin2(in_2), .pin3(in_3), .pin4(1'b0), .pin5(1'b0), .pin6(nand_2_out), .pin7(nRDREG_HL),
    .pin8(1'b0), .pin9(nRDREGL), .pin10(nRDREGH), .pin11(nRDREGE), .pin12(nRDREGD), .pin13(nRDREGC),
    .pin14(nRDREGB), .pin15(nRDREGA), .pin16(1'b1));
  _74138 _74138_2 (
    .pin1(and_3_out), .pin2(and_4_out), .pin3(and_5_out), .pin4(1'b0), .pin5(1'b0), .pin6(nand_2_out),
    .pin7(nWRREG_HL), .pin8(1'b0), .pin9(nWRREGL), .pin10(nWRREGH), .pin11(nWRREGE), .pin12(nWRREGD),
    .pin13(nWRREGC), .pin14(nWRREGB), .pin15(nWRREGA), .pin16(1'b1));
  LED DEC (.in(_74540_2_pin16));
  LED JPcc (.in(_74540_2_pin15));
  LED CALLcc (.in(_74540_2_pin14));
  LED JPnn (.in(_74540_2_pin13));
  LED CALLnn (.in(_74540_2_pin12));
  LED LD_IMM (.in(not_3_out));
  not not_3 (not_3_out, nOPIMMLD);
  _74540 _74540_3 (
    .pin1(1'b0), .pin2(nNC), .pin3(nNZ), .pin4(nC), .pin5(nZ), .pin6(nPE), .pin7(nPO), .pin8(nP), .pin9(nM),
    .pin10(1'b0), .pin11(_74540_3_pin11), .pin12(_74540_3_pin12), .pin13(_74540_3_pin13),
    .pin14(_74540_3_pin14), .pin15(_74540_3_pin15), .pin16(_74540_3_pin16), .pin17(_74540_3_pin17),
    .pin18(_74540_3_pin18), .pin19(1'b0), .pin20(1'b1));
  LED u_NC (.in(_74540_3_pin18));
  _74138 _74138_3 (
    .pin1(in_1), .pin2(in_2), .pin3(in_3), .pin4(nTYPE0), .pin5(nTYPE0), .pin6(1'b1), .pin7(nOPRET),
    .pin8(1'b0), .pin9(nOPIMMLD), .pin10(nOPRST), .pin11(nOPIMMALU), .pin12(nOPRETcc), .pin13(nOPSHIFT),
    .pin14(nOPDEC), .pin15(nOPINC), .pin16(1'b1));
  _74138 _74138_4 (
    .pin1(in_1), .pin2(in_2), .pin3(in_3), .pin4(nTYPE1), .pin5(nTYPE1), .pin6(1'b1), .pin7(nOPI_O3),
    .pin8(1'b0), .pin9(nOPCALLnn), .pin10(nOPI_O2), .pin11(nOPJPnn), .pin12(nOPI_O1), .pin13(nOPCALLcc),
    .pin14(nOPI_O0), .pin15(nOPJPcc), .pin16(1'b1));
  LED u_NZ (.in(_74540_3_pin17));
  LED C (.in(_74540_3_pin16));
  LED Z (.in(_74540_3_pin15));
  LED PE (.in(_74540_3_pin14));
  LED PO (.in(_74540_3_pin13));
  LED P (.in(_74540_3_pin12));
  LED M (.in(_74540_3_pin11));
  LED RLCA (.in(not_4_out));
  LED RRCA (.in(not_5_out));
  not not_4 (not_4_out, nRLCA);
  not not_5 (not_5_out, nRRCA);
  _74139 _74139_1 (
    .pin1(nOPSHIFT), .pin2(in_4), .pin3(in_5), .pin4(nRLCA), .pin5(nRRCA), .pin6(nRLA), .pin7(nRRA),
    .pin8(1'b0), .pin9(nTYPE3), .pin10(nTYPE2), .pin11(nTYPE1), .pin12(nTYPE0), .pin13(in_8), .pin14(in_7),
    .pin15(1'b0), .pin16(1'b1));
  _74138 _74138_5 (
    .pin1(in_4), .pin2(in_5), .pin3(in_6), .pin4(nTYPE2), .pin5(nTYPE2), .pin6(1'b1), .pin7(nALUCP),
    .pin8(1'b0), .pin9(nALUOR), .pin10(nALUXOR), .pin11(nALUAND), .pin12(nALUSBC), .pin13(nALUSUB),
    .pin14(nALUADC), .pin15(nALUADD), .pin16(1'b1));
  LED RLA (.in(not_6_out));
  LED RRA (.in(not_7_out));
  not not_6 (not_6_out, nRLA);
  not not_7 (not_7_out, nRRA);
  _74540 _74540_4 (
    .pin1(1'b0), .pin2(nWRREGA), .pin3(nWRREGB), .pin4(nWRREGC), .pin5(nWRREGD), .pin6(nWRREGE),
    .pin7(nWRREGH), .pin8(nWRREGL), .pin9(nWRREG_HL), .pin10(1'b0), .pin11(_74540_4_pin11),
    .pin12(_74540_4_pin12), .pin13(_74540_4_pin13), .pin14(_74540_4_pin14), .pin15(_74540_4_pin15),
    .pin16(_74540_4_pin16), .pin17(_74540_4_pin17), .pin18(_74540_4_pin18), .pin19(1'b0), .pin20(1'b1));
  LED B (.in(_74540_4_pin17));
  LED A (.in(_74540_4_pin18));
  LED D (.in(_74540_4_pin15));
  LED C_2 (.in(_74540_4_pin16));
  LED H (.in(_74540_4_pin13));
  LED E (.in(_74540_4_pin14));
  nand nand_3 (nand_3_out, nOPRETcc, nOPCALLcc, nOPJPcc);
  LED HL (.in(_74540_4_pin11));
  LED L (.in(_74540_4_pin12));
  _74540 _74540_5 (
    .pin1(1'b0), .pin2(nRDREGA), .pin3(nRDREGB), .pin4(nRDREGC), .pin5(nRDREGD), .pin6(nRDREGE),
    .pin7(nRDREGH), .pin8(nRDREGL), .pin9(nRDREG_HL), .pin10(1'b0), .pin11(_74540_5_pin11),
    .pin12(_74540_5_pin12), .pin13(_74540_5_pin13), .pin14(_74540_5_pin14), .pin15(_74540_5_pin15),
    .pin16(_74540_5_pin16), .pin17(_74540_5_pin17), .pin18(_74540_5_pin18), .pin19(1'b0), .pin20(1'b1));
  _74138 _74138_6 (
    .pin1(in_4), .pin2(in_5), .pin3(in_6), .pin4(1'b0), .pin5(1'b0), .pin6(nand_3_out), .pin7(nM),
    .pin8(1'b0), .pin9(nP), .pin10(nPO), .pin11(nPE), .pin12(nZ), .pin13(nC), .pin14(nNZ), .pin15(nNC),
    .pin16(1'b1));
  LED A_2 (.in(_74540_5_pin18));
  LED C_3 (.in(_74540_5_pin16));
  LED B_2 (.in(_74540_5_pin17));
  LED E_2 (.in(_74540_5_pin14));
  LED D_2 (.in(_74540_5_pin15));
  LED L_2 (.in(_74540_5_pin12));
  LED H_2 (.in(_74540_5_pin13));
  LED HL_2 (.in(_74540_5_pin11));

  // Other names for the same wires on the sheet: IR0 = in_1; IR1 = in_2; IR2 = in_3; IR3 = in_4; IR4 = in_5;
  //   IR5 = in_6; IR6 = in_7; IR7 = in_8

  // Notes on the sheet:
  //   INSTRUCTION DECODER
  //   ALU OP
  //   CONDITION
  //   SHIFT
  //   DESTINATION
  //   SOURCE
endmodule
